// Logisim project 16 Bit ALU.circ as structural Verilog: 2 circuits, main circuit 16 Bit ALU
module _16_Bit_ALU (
  input  B_Invert,
  input  [15:0] Input_A,
  input  [15:0] Input_B,
  input  [1:0] ALU_Op,
  output Zero_Flag,
  output [15:0] ALU_Output,
  output Overflow_Flag,
  output C_Out
);

  wire _0_c_out, _1_c_out, _2_c_out, _3_c_out, _4_c_out, _5_c_out, _6_c_out, _7_c_out, _8_c_out, _9_c_out,
       _10_c_out, _11_c_out, _12_c_out, _13_c_out, _14_c_out;

  _1_Bit_ALU _0 (
    .B(Input_B[0]), .A(Input_A[0]), .ALU_Output(ALU_Output[0]), .C_in(B_Invert), .ALU_Op(ALU_Op),
    .B_Invert(B_Invert), .C_out(_0_c_out));
  _1_Bit_ALU _1 (
    .B(Input_B[1]), .A(Input_A[1]), .ALU_Output(ALU_Output[1]), .C_in(_0_c_out), .ALU_Op(ALU_Op),
    .B_Invert(B_Invert), .C_out(_1_c_out));
  _1_Bit_ALU _2 (
    .B(Input_B[2]), .A(Input_A[2]), .ALU_Output(ALU_Output[2]), .C_in(_1_c_out), .ALU_Op(ALU_Op),
    .B_Invert(B_Invert), .C_out(_2_c_out));
  _1_Bit_ALU _3 (
    .B(Input_B[3]), .A(Input_A[3]), .ALU_Output(ALU_Output[3]), .C_in(_2_c_out), .ALU_Op(ALU_Op),
    .B_Invert(B_Invert), .C_out(_3_c_out));
  _1_Bit_ALU _4 (
    .B(Input_B[4]), .A(Input_A[4]), .ALU_Output(ALU_Output[4]), .C_in(_3_c_out), .ALU_Op(ALU_Op),
    .B_Invert(B_Invert), .C_out(_4_c_out));
  _1_Bit_ALU _5 (
    .B(Input_B[5]), .A(Input_A[5]), .ALU_Output(ALU_Output[5]), .C_in(_4_c_out), .ALU_Op(ALU_Op),
    .B_Invert(B_Invert), .C_out(_5_c_out));
  _1_Bit_ALU _6 (
    .B(Input_B[6]), .A(Input_A[6]), .ALU_Output(ALU_Output[6]), .C_in(_5_c_out), .ALU_Op(ALU_Op),
    .B_Invert(B_Invert), .C_out(_6_c_out));
  _1_Bit_ALU _7 (
    .B(Input_B[7]), .A(Input_A[7]), .ALU_Output(ALU_Output[7]), .C_in(_6_c_out), .ALU_Op(ALU_Op),
    .B_Invert(B_Invert), .C_out(_7_c_out));
  _1_Bit_ALU _8 (
    .B(Input_B[8]), .A(Input_A[8]), .ALU_Output(ALU_Output[8]), .C_in(_7_c_out), .ALU_Op(ALU_Op),
    .B_Invert(B_Invert), .C_out(_8_c_out));
  _1_Bit_ALU _9 (
    .B(Input_B[9]), .A(Input_A[9]), .ALU_Output(ALU_Output[9]), .C_in(_8_c_out), .ALU_Op(ALU_Op),
    .B_Invert(B_Invert), .C_out(_9_c_out));
  _1_Bit_ALU _10 (
    .B(Input_B[10]), .A(Input_A[10]), .ALU_Output(ALU_Output[10]), .C_in(_9_c_out), .ALU_Op(ALU_Op),
    .B_Invert(B_Invert), .C_out(_10_c_out));
  _1_Bit_ALU _11 (
    .B(Input_B[11]), .A(Input_A[11]), .ALU_Output(ALU_Output[11]), .C_in(_10_c_out), .ALU_Op(ALU_Op),
    .B_Invert(B_Invert), .C_out(_11_c_out));
  _1_Bit_ALU _12 (
    .B(Input_B[12]), .A(Input_A[12]), .ALU_Output(ALU_Output[12]), .C_in(_11_c_out), .ALU_Op(ALU_Op),
    .B_Invert(B_Invert), .C_out(_12_c_out));
  _1_Bit_ALU _13 (
    .B(Input_B[13]), .A(Input_A[13]), .ALU_Output(ALU_Output[13]), .C_in(_12_c_out), .ALU_Op(ALU_Op),
    .B_Invert(B_Invert), .C_out(_13_c_out));
  _1_Bit_ALU _14 (
    .B(Input_B[14]), .A(Input_A[14]), .ALU_Output(ALU_Output[14]), .C_in(_13_c_out), .ALU_Op(ALU_Op),
    .B_Invert(B_Invert), .C_out(_14_c_out));
  _1_Bit_ALU _15 (
    .B(Input_B[15]), .A(Input_A[15]), .ALU_Output(ALU_Output[15]), .C_in(_14_c_out), .ALU_Op(ALU_Op),
    .B_Invert(B_Invert), .C_out(C_Out));
  xor xor_1 (Overflow_Flag, _14_c_out, C_Out);
  nor nor_1 (Zero_Flag, ALU_Output[0], ALU_Output[1], ALU_Output[2], ALU_Output[3], ALU_Output[4], ALU_Output[5], ALU_Output[6], ALU_Output[7], ALU_Output[8], ALU_Output[9], ALU_Output[10], ALU_Output[11], ALU_Output[12], ALU_Output[13], ALU_Output[14], ALU_Output[15]);

  // Notes on the sheet:
  //   C_In
endmodule

module _1_Bit_ALU (
  input  B,
  input  A,
  input  C_in,
  input  [1:0] ALU_Op,
  input  B_Invert,
  output ALU_Output,
  output C_out
);

  wire adder_1_out, and_1_out, multiplexer_1_out, not_1_out, or_1_out;

  not not_1 (not_1_out, B);
  Multiplexer #(.enable("false")) multiplexer_1 (.in0(B), .in1(not_1_out), .out(multiplexer_1_out), .sel(B_Invert));
  and and_1 (and_1_out, A, B);
  or or_1 (or_1_out, A, B);
  Adder #(.width(1)) adder_1 (.a(A), .b(multiplexer_1_out), .out(adder_1_out), .cin(C_in), .cout(C_out));
  Multiplexer #(.select(2), .enable("false")) multiplexer_2 (
    .in0(and_1_out), .in1(or_1_out), .in2(adder_1_out), .out(ALU_Output), .sel(ALU_Op));  // open: in3
endmodule
