// Logisim project 16 Bit Single Cycle MIPS CPU.circ as structural Verilog: 1 circuit, main circuit 16 Bits MIPS
module _16_Bits_MIPS (
  input  in_1,
  input  in_2
);

  wire and_1_out, CLK_out, control_unit_1_alusrc, control_unit_1_branch, control_unit_1_jump,
       control_unit_1_memread, control_unit_1_memtoreg, control_unit_1_memwrite, control_unit_1_regdst,
       control_unit_1_regwrite, n16_bit_alu_1_zero_flag;
  wire [1:0] alu_control_unit_1_out_3, control_unit_1_aluop;
  wire [2:0] multiplexer_1_out;
  wire [3:2] alu_control_unit_1_out_3_2;
  wire [15:0] adder_1_out, adder_2_out, jump_address_extend_1_jump_address, multiplexer_2_out,
       multiplexer_3_out, multiplexer_4_out, multiplexer_5_out, n16_bit_alu_1_alu_output,
       n16_bit_register_file_1_read_data_1, n16_bit_register_file_1_read_data_2, PC_q, ram_1_data,
       rom_1_data, sign_extend_1_sign_extended_value;

  Register #(.width(16)) PC (.D(multiplexer_4_out), .Q(PC_q), .clk(CLK_out));  // open: en, clr
  Adder #(.width(16)) adder_1 (.a(PC_q), .b(16'h1), .out(adder_1_out), .cin(in_2));  // open: cout
  ROM #(.addrWidth(16), .dataWidth(16)) rom_1 (.addr(PC_q), .data(rom_1_data));  // open: sel
  Jump_Address_Extend jump_address_extend_1 (
    .Immediate_Value(rom_1_data[12:0]), .PC_Input(adder_1_out[15:13]),
    .Jump_Address(jump_address_extend_1_jump_address));
  Multiplexer #(.width(3), .enable("false")) multiplexer_1 (
    .in0(rom_1_data[9:7]), .in1(rom_1_data[6:4]), .out(multiplexer_1_out), .sel(control_unit_1_regdst));
  Control_Unit control_unit_1 (
    .Op_2(rom_1_data[15]), .Op_1(rom_1_data[14]), .Op_0(rom_1_data[13]), .RegDst(control_unit_1_regdst),
    .RegWrite(control_unit_1_regwrite), .ALUSrc(control_unit_1_alusrc), .MemRead(control_unit_1_memread),
    .MemWrite(control_unit_1_memwrite), .Branch(control_unit_1_branch), .Jump(control_unit_1_jump),
    .ALUOp(control_unit_1_aluop), .MemtoReg(control_unit_1_memtoreg));
  Sign_Extend sign_extend_1 (
    .Immediate_Value(rom_1_data[6:0]), .Sign_Extended_Value(sign_extend_1_sign_extended_value));
  _16_Bit__Register_File u_16_bit_register_file_1 (
    .Write_Data(multiplexer_5_out), .Read_Data_1(n16_bit_register_file_1_read_data_1),
    .Read_Register_1(rom_1_data[12:10]), .Read_Data_2(n16_bit_register_file_1_read_data_2),
    .Read_Register_2(rom_1_data[9:7]), .RegWrite(control_unit_1_regwrite), .CLK(CLK_out),
    .Write_Register(multiplexer_1_out));
  Clock CLK (.out(CLK_out));
  Adder #(.width(16)) adder_2 (
    .a(adder_1_out), .b(sign_extend_1_sign_extended_value), .out(adder_2_out), .cin(in_1));  // open: cout
  Multiplexer #(.width(16), .enable("false")) multiplexer_2 (
    .in0(n16_bit_register_file_1_read_data_2), .in1(sign_extend_1_sign_extended_value),
    .out(multiplexer_2_out), .sel(control_unit_1_alusrc));
  ALU_Control_Unit alu_control_unit_1 (
    .ALUOP(control_unit_1_aluop), .Function(rom_1_data[3:0]),
    .out_3({alu_control_unit_1_out_3_2, alu_control_unit_1_out_3}));
  Multiplexer #(.width(16), .enable("false")) multiplexer_3 (
    .in0(adder_1_out), .in1(adder_2_out), .out(multiplexer_3_out), .sel(and_1_out));
  _16_Bit_ALU u_16_bit_alu_1 (
    .Input_A(n16_bit_register_file_1_read_data_1), .Input_B(multiplexer_2_out),
    .Zero_Flag(n16_bit_alu_1_zero_flag), .ALU_Output(n16_bit_alu_1_alu_output),
    .B_Invert(alu_control_unit_1_out_3_2[2]), .ALU_Op(alu_control_unit_1_out_3));  // open: Overflow_Flag, C_Out
  and and_1 (and_1_out, control_unit_1_branch, n16_bit_alu_1_zero_flag);
  Multiplexer #(.width(16), .enable("false")) multiplexer_4 (
    .in0(multiplexer_3_out), .in1(jump_address_extend_1_jump_address), .out(multiplexer_4_out),
    .sel(control_unit_1_jump));
  RAM #(.addrWidth(16), .dataWidth(16), .bus("separate")) ram_1 (
    .addr(n16_bit_alu_1_alu_output), .din(n16_bit_register_file_1_read_data_2), .data(ram_1_data),
    .str(control_unit_1_memwrite), .clk(CLK_out), .ld(control_unit_1_memread));  // open: sel, clr
  Multiplexer #(.width(16), .enable("false")) multiplexer_5 (
    .in0(n16_bit_alu_1_alu_output), .in1(ram_1_data), .out(multiplexer_5_out), .sel(control_unit_1_memtoreg));
endmodule
