// Logisim project ALU Control Unit.circ as structural Verilog: 1 circuit, main circuit ALU Control Unit
module ALU_Control_Unit (
  input  [1:0] ALUOP,
  input  [3:0] Function,
  output [3:0] out_3
);

  wire and_1_out, not_1_out, not_2_out;

  and and_1 (and_1_out, ALUOP[1], Function[1]);
  or or_1 (out_3[2], ALUOP[0], and_1_out);
  not not_1 (not_1_out, ALUOP[1]);
  not not_2 (not_2_out, Function[2]);
  or or_2 (out_3[1], not_1_out, not_2_out);
  and and_2 (out_3[0], ALUOP[1], Function[0]);

  assign out_3[3] = 1'b0;

  // Notes on the sheet:
  //   ALUCtrl-2
  //   ALUCtrl-1
  //   ALUCtrl-3
  //   ALUCtrl-0
endmodule
