// Logisim project Control Unit.circ as structural Verilog: 1 circuit, main circuit Control Unit
module Control_Unit (
  input  Op_2,
  input  Op_1,
  input  Op_0,
  output RegDst,
  output RegWrite,
  output ALUSrc,
  output MemRead,
  output MemWrite,
  output Branch,
  output MemtoReg,
  output [1:0] ALUOp,
  output Jump
);

  wire not_1_out, not_2_out, not_3_out, not_4_out, not_5_out, not_6_out, not_7_out, not_8_out, not_9_out,
       not_10_out;

  not not_1 (not_1_out, Op_2);
  not not_2 (not_2_out, Op_1);
  not not_3 (not_3_out, Op_0);
  not not_4 (not_4_out, Op_2);
  not not_5 (not_5_out, Op_1);
  not not_6 (not_6_out, Op_2);
  not not_7 (not_7_out, Op_0);
  not not_8 (not_8_out, Op_2);
  not not_9 (not_9_out, Op_1);
  not not_10 (not_10_out, Op_0);
  and R_type (ALUOp[1], not_1_out, not_2_out, not_3_out);
  and LW (MemRead, not_4_out, not_5_out, Op_0);
  and SW (MemWrite, not_6_out, Op_1, not_7_out);
  and Beq (ALUOp[0], not_8_out, Op_1, Op_0);
  and u_Jump (Jump, Op_2, not_9_out, not_10_out);
  or or_1 (RegWrite, ALUOp[1], MemRead);
  or or_2 (ALUSrc, MemRead, MemWrite);

  assign Branch = ALUOp[0];
  assign MemtoReg = MemRead;
  assign RegDst = ALUOp[1];
endmodule
