// Logisim project Jump Address Extend.circ as structural Verilog: 1 circuit, main circuit Jump Address Extend
module Jump_Address_Extend (
  input  [12:0] Immediate_Value,
  input  [2:0] PC_Input,
  output [15:0] Jump_Address
);


  assign Jump_Address = {PC_Input, Immediate_Value};
endmodule
