// Logisim project Sign Extend.circ as structural Verilog: 1 circuit, main circuit Sign Extend
module Sign_Extend (
  input  [6:0] Immediate_Value,
  output [15:0] Sign_Extended_Value
);


  assign Sign_Extended_Value = {{10{Immediate_Value[6]}}, Immediate_Value[5:0]};
endmodule
